// Logisim project D flip flop från 2 D Latch.circ as structural Verilog: 1 circuit, main circuit main
module main (
  input  in_1,
  output out_2
);

  wire and_1_out, and_2_out, and_3_out, and_4_out, not_1_out, not_2_out, undriven, undriven_2, undriven_3,
       undriven_4, undriven_5;

  not not_1 (not_1_out, undriven_4);
  not not_2 (not_2_out, undriven_5);
  and and_1 (and_1_out, in_1, not_1_out, not_2_out);
  and and_2 (and_2_out, undriven, not_1_out, undriven_5);
  and and_3 (and_3_out, undriven_2, undriven_4, not_2_out);
  and and_4 (and_4_out, undriven_3, undriven_4, undriven_5);
  or or_1 (out_2, and_1_out, and_2_out, and_3_out, and_4_out);
endmodule
