// Logisim project labb 3 utan mux.circ as structural Verilog: 1 circuit, main circuit main
module main (
  input  in_1,
  input  in_2,
  output out_3,
  output out_4,
  output out_5,
  output out_6,
  output out_7,
  output out_8
);

  wire and_1_out, and_2_out, and_3_out, button_1_out, not_1_out, not_2_out, or_1_out, or_2_out, or_3_out,
       or_4_out;

  not not_1 (not_1_out, in_1);
  not not_2 (not_2_out, in_2);
  or or_1 (or_1_out, out_6, out_4, in_2);
  and and_1 (and_1_out, not_1_out, out_4);
  and and_2 (and_2_out, in_1, not_2_out, out_3);
  or or_2 (or_2_out, not_1_out, out_7);
  or or_3 (or_3_out, in_1, not_2_out, out_6, out_3);
  or or_4 (or_4_out, and_1_out, and_2_out);
  and and_3 (and_3_out, or_2_out, or_3_out);
  or or_5 (out_5, or_4_out, out_7);
  and and_4 (out_8, and_3_out, or_1_out);
  Button button_1 (.out(button_1_out));
  D_Flip_Flop d_ff_1 (.clk(button_1_out), .D(out_5), .Q(out_3), .Qn(out_4));  // open: preset, en, reset
  D_Flip_Flop d_ff_2 (.clk(button_1_out), .D(out_8), .Q(out_6), .Qn(out_7));  // open: preset, en, reset

  // Notes on the sheet:
  //   q1'
  //   q1
  //   q0'
  //   q0
  //   A
  //   B
  //   A'
  //   B'
endmodule
