// Logisim project labb 3.circ as structural Verilog: 1 circuit, main circuit main
module main (
  input  [1:0] A_B,
  output Q,
  output out_3,
  output Q_prime,
  output Q_2,
  output out_6,
  output Q_prime_2
);

  wire button_1_out, nand_1_out, nand_2_out, not_1_out, or_1_out, or_2_out, or_3_out;

  nand nand_1 (nand_1_out, Q, Q_2);
  nand nand_2 (nand_2_out, Q_prime, Q_2);
  or or_1 (or_1_out, Q_prime, Q_2);
  or or_2 (or_2_out, Q_2, Q);
  or or_3 (or_3_out, Q, Q_2);
  not not_1 (not_1_out, or_3_out);
  Multiplexer #(.select(2)) multiplexer_1 (
    .in0(nand_1_out), .in1(nand_1_out), .in2(nand_2_out), .in3(Q_prime_2), .out(out_3), .sel(A_B));  // open: en
  Multiplexer #(.select(2)) multiplexer_2 (
    .in0(or_1_out), .in1(or_2_out), .in2(not_1_out), .in3(Q_prime_2), .out(out_6), .sel(A_B));  // open: en
  Button button_1 (.out(button_1_out));
  D_Flip_Flop d_ff_1 (.clk(button_1_out), .D(out_3), .Q(Q), .Qn(Q_prime));  // open: preset, en, reset
  D_Flip_Flop d_ff_2 (.clk(button_1_out), .D(out_6), .Q(Q_2), .Qn(Q_prime_2));  // open: preset, en, reset

  // Notes on the sheet:
  //   q1
  //   q0
  //   q0'
  //   q1'
  //   q1+
  //   q0+
endmodule
